# Fritzing sketch ZumoGruppeNut (saved by Fritzing 0.9.3b)
breadboards: 3

parts:
  Part1 = Arduino Uno (Rev3)
  hc-sr1 = hc-sr04
  hc-sr2 = hc-sr04
  hc-sr3 = hc-sr04
  Part2 = Bluetooth HC-05 Macho

nets:
  N1: Part1.A1, hc-sr2.Echo
  N2: Part1.A4/SDA, Part2.TXD
  N3: Part1.A5/SCL, Part2.RXD
  N4: Part1.D0/RX, hc-sr3.Echo
  N5: Part1.D3_PWM, hc-sr1.Echo
  N6: Part1.D6_PWM, hc-sr1.Trig, hc-sr2.Trig, hc-sr3.Trig, Part2.GND
  VCC: Part1.5V, hc-sr1.VCC, hc-sr2.VCC, hc-sr3.VCC, Part2.VCC
  GND: Part1.GND, hc-sr1.GND, hc-sr2.GND, hc-sr3.GND
